// Digital circuit 299_demo_6.dig as structural Verilog
module _299_demo_6 (
  input  CLK,
  input  in_2,
  input  in_3,
  input  in_4,
  input  in_5,
  input  in_6,
  input  in_7,
  input  in_8,
  input  in_9,
  input  in_10,
  input  in_11,
  input  in_12,
  input  in_13,
  input  in_14
);

  wire button_1_out, button_2_out, button_3_out, button_4_out, button_5_out, button_6_out, button_7_out,
       button_8_out, button_9_out, button_10_out, button_11_out, button_12_out, button_13_out, button_14_out,
       button_15_out, button_16_out, button_17_out, d_ff_1_nq, d_ff_2_nq, d_ff_3_nq, d_ff_4_nq, d_ff_5_nq,
       d_ff_6_nq, d_ff_7_nq, d_ff_8_nq, d_ff_9_nq, d_ff_10_nq, d_ff_11_nq, d_ff_12_nq, d_ff_13_nq,
       d_ff_14_nq, d_ff_15_nq, d_ff_16_nq, IC2_pin2, IC2_pin3, IC2_pin6, IC2_pin8, IC2_pin9, IC2_pin10,
       IC3_pin4, IC3_pin5, IC3_pin8, IC3_pin9, IC5_pin8, IC5_pin18, IC13_pin13, IC13_pin15, IC14_pin11,
       not_2_out;
  wire [3:0] _74299_1_pin5, _74299_1_pin6, d_ff_9_q, IC5_pin6, IC5_pin16, IC6_pin5, IC6_pin6, IC7_pin6,
       IC13_pin5, IC13_pin14, IC14_pin4, IC14_pin15;

  _7474 IC2 (
    .pin1(1'b1), .pin2(IC2_pin2), .pin3(IC2_pin3), .pin4(1'b1), .pin6(IC2_pin6), .pin7(1'b0),
    .pin8(IC2_pin8), .pin9(IC2_pin9), .pin10(IC2_pin10), .pin11(1'b1), .pin12(IC2_pin8), .pin13(IC2_pin6),
    .pin14(1'b1));  // open: pin5
  // Probe SS on IC2_pin8
  _7400 IC3 (
    .pin1(CLK), .pin2(CLK), .pin3(IC2_pin3), .pin4(IC3_pin4), .pin5(IC3_pin5), .pin6(IC2_pin10), .pin7(1'b0),
    .pin8(IC3_pin8), .pin9(IC3_pin9), .pin10(IC3_pin9), .pin11(IC3_pin9), .pin12(IC2_pin8), .pin13(CLK),
    .pin14(1'b1));
  LED led_1 (.in(IC13_pin5[3]));
  LED led_2 (.in(IC13_pin5[2]));
  D_FF d_ff_1 (.D(d_ff_1_nq), .C(button_1_out), .Q(IC13_pin5[3]), .nQ(d_ff_1_nq));
  Button button_1 (.out(button_1_out));
  LED led_3 (.in(IC13_pin5[1]));
  D_FF d_ff_2 (.D(d_ff_2_nq), .C(button_2_out), .Q(IC13_pin5[2]), .nQ(d_ff_2_nq));
  Button button_2 (.out(button_2_out));
  _74163 IC1 (
    .pin1(IC2_pin8), .pin2(CLK), .pin3(1'b0), .pin4(1'b0), .pin5(1'b0), .pin6(1'b0), .pin7(IC2_pin8),
    .pin8(1'b0), .pin9(1'b1), .pin10(1'b1), .pin11(IC3_pin5), .pin14(IC3_pin4), .pin16(1'b1));  // open: pin12, pin13, pin15
  LED led_4 (.in(IC13_pin5[0]));
  D_FF d_ff_3 (.D(d_ff_3_nq), .C(button_3_out), .Q(IC13_pin5[1]), .nQ(d_ff_3_nq));
  Button button_3 (.out(button_3_out));
  _74166 IC13 (
    .pin1(1'b0), .pin2(IC13_pin5[3]), .pin3(IC13_pin5[2]), .pin4(IC13_pin5[1]), .pin5(IC13_pin5[0]),
    .pin6(1'b0), .pin7(IC3_pin8), .pin8(1'b0), .pin9(1'b1), .pin10(IC13_pin14[3]), .pin11(IC13_pin14[2]),
    .pin12(IC13_pin14[1]), .pin13(IC13_pin13), .pin14(IC13_pin14[0]), .pin15(IC13_pin15), .pin16(1'b1));
  LED led_5 (.in(IC13_pin14[3]));
  D_FF d_ff_4 (.D(d_ff_4_nq), .C(button_4_out), .Q(IC13_pin5[0]), .nQ(d_ff_4_nq));
  Button button_4 (.out(button_4_out));
  LED led_6 (.in(IC13_pin14[2]));
  D_FF d_ff_5 (.D(d_ff_5_nq), .C(button_5_out), .Q(IC13_pin14[3]), .nQ(d_ff_5_nq));
  Button button_5 (.out(button_5_out));
  LED led_7 (.in(IC13_pin14[1]));
  D_FF d_ff_6 (.D(d_ff_6_nq), .C(button_6_out), .Q(IC13_pin14[2]), .nQ(d_ff_6_nq));
  Button button_6 (.out(button_6_out));
  LED led_8 (.in(IC13_pin14[0]));
  D_FF d_ff_7 (.D(d_ff_7_nq), .C(button_7_out), .Q(IC13_pin14[1]), .nQ(d_ff_7_nq));
  Button button_7 (.out(button_7_out));
  Seven_Seg_Hex seven_seg_hex_1 (.d(IC13_pin5), .dp(1'b0));
  D_FF d_ff_8 (.D(d_ff_8_nq), .C(button_8_out), .Q(IC13_pin14[0]), .nQ(d_ff_8_nq));
  Button button_8 (.out(button_8_out));
  Seven_Seg_Hex seven_seg_hex_2 (.d(IC13_pin14), .dp(1'b0));
  _74595 IC14 (
    .pin1(IC14_pin15[2]), .pin2(IC14_pin15[1]), .pin3(IC14_pin15[0]), .pin4(IC14_pin4[3]),
    .pin5(IC14_pin4[2]), .pin6(IC14_pin4[1]), .pin7(IC14_pin4[0]), .pin8(1'b0), .pin9(IC13_pin13),
    .pin10(1'b1), .pin11(IC14_pin11), .pin12(IC3_pin8), .pin13(1'b0), .pin15(IC14_pin15[3]), .pin16(1'b1));  // open: pin14
  not not_1 (IC14_pin11, IC2_pin8);
  Seven_Seg_Hex seven_seg_hex_3 (.d(IC14_pin15), .dp(1'b0));
  Seven_Seg_Hex seven_seg_hex_4 (.d(IC14_pin4), .dp(1'b0));
  Monoflop monoflop_1 (.C(IC2_pin8), .R(IC3_pin8), .nQ(IC13_pin15));  // open: Q
  _74299 _74299_1 (
    .pin1(in_2), .pin2(in_3), .pin3(in_4), .pin4(_74299_1_pin5[2]), .pin5(_74299_1_pin5[0]),
    .pin6(_74299_1_pin6[2]), .pin7(_74299_1_pin6[0]), .pin9(in_5), .pin10(1'b0), .pin11(in_8),
    .pin12(IC3_pin8), .pin13(_74299_1_pin6[1]), .pin14(_74299_1_pin6[3]), .pin15(_74299_1_pin5[1]),
    .pin16(_74299_1_pin5[3]), .pin18(in_13), .pin19(IC13_pin15), .pin20(1'b1));  // open: pin8, pin17
  LED led_9 (.in(_74299_1_pin5[3]));
  LED led_10 (.in(_74299_1_pin5[2]));
  LED led_11 (.in(_74299_1_pin5[1]));
  LED led_12 (.in(_74299_1_pin5[0]));
  LED led_13 (.in(_74299_1_pin6[3]));
  LED led_14 (.in(_74299_1_pin6[2]));
  LED led_15 (.in(_74299_1_pin6[1]));
  Seven_Seg_Hex seven_seg_hex_5 (.d(_74299_1_pin5), .dp(1'b0));
  LED led_16 (.in(_74299_1_pin6[0]));
  Seven_Seg_Hex seven_seg_hex_6 (.d(_74299_1_pin6), .dp(1'b0));
  not not_2 (not_2_out, IC13_pin15);
  _74299 IC5 (
    .pin1(not_2_out), .pin2(in_6), .pin3(in_7), .pin4(IC5_pin16[2]), .pin5(IC5_pin16[0]), .pin6(IC5_pin6[2]),
    .pin7(IC5_pin6[0]), .pin8(IC5_pin8), .pin9(1'b1), .pin10(1'b0), .pin11(in_14), .pin12(IC3_pin8),
    .pin13(IC5_pin6[1]), .pin14(IC5_pin6[3]), .pin15(IC5_pin16[1]), .pin16(IC5_pin16[3]), .pin18(IC5_pin18),
    .pin19(1'b1), .pin20(1'b1));  // open: pin17
  Button button_9 (.out(button_9_out));
  Monoflop #(.timerDelay(2)) monoflop_2 (.C(button_9_out), .R(1'b0), .Q(IC2_pin2));  // open: nQ
  D_FF d_ff_9 (.D(d_ff_9_nq), .C(button_10_out), .Q(d_ff_9_q[3]), .nQ(d_ff_9_nq));
  _74541 IC7 (
    .pin1(IC13_pin15), .pin2(d_ff_9_q[3]), .pin3(d_ff_9_q[2]), .pin4(d_ff_9_q[1]), .pin5(d_ff_9_q[0]),
    .pin6(IC7_pin6[3]), .pin7(IC7_pin6[2]), .pin8(IC7_pin6[1]), .pin9(IC7_pin6[0]), .pin10(1'b0),
    .pin11(IC5_pin6[0]), .pin12(IC5_pin6[1]), .pin13(IC5_pin6[2]), .pin14(IC5_pin6[3]), .pin15(IC5_pin16[0]),
    .pin16(IC5_pin16[1]), .pin17(IC5_pin16[2]), .pin18(IC5_pin16[3]), .pin19(IC13_pin15), .pin20(1'b1));
  D_FF d_ff_10 (.D(d_ff_10_nq), .C(button_11_out), .Q(d_ff_9_q[2]), .nQ(d_ff_10_nq));
  Button button_10 (.out(button_10_out));
  LED led_17 (.in(IC5_pin16[3]));
  LED led_18 (.in(IC5_pin16[2]));
  D_FF d_ff_11 (.D(d_ff_11_nq), .C(button_12_out), .Q(d_ff_9_q[1]), .nQ(d_ff_11_nq));
  Button button_11 (.out(button_11_out));
  LED led_19 (.in(IC5_pin16[1]));
  LED led_20 (.in(IC5_pin16[0]));
  D_FF d_ff_12 (.D(d_ff_12_nq), .C(button_13_out), .Q(d_ff_9_q[0]), .nQ(d_ff_12_nq));
  Button button_12 (.out(button_12_out));
  LED led_21 (.in(IC5_pin6[3]));
  LED led_22 (.in(IC5_pin6[2]));
  D_FF d_ff_13 (.D(d_ff_13_nq), .C(button_14_out), .Q(IC7_pin6[3]), .nQ(d_ff_13_nq));
  Button button_13 (.out(button_13_out));
  LED led_23 (.in(IC5_pin6[1]));
  LED led_24 (.in(IC5_pin6[0]));
  D_FF d_ff_14 (.D(d_ff_14_nq), .C(button_15_out), .Q(IC7_pin6[2]), .nQ(d_ff_14_nq));
  Button button_14 (.out(button_14_out));
  Seven_Seg_Hex seven_seg_hex_7 (.d(IC5_pin16), .dp(1'b0));
  D_FF d_ff_15 (.D(d_ff_15_nq), .C(button_16_out), .Q(IC7_pin6[1]), .nQ(d_ff_15_nq));
  Button button_15 (.out(button_15_out));
  Seven_Seg_Hex seven_seg_hex_8 (.d(IC5_pin6), .dp(1'b0));
  D_FF d_ff_16 (.D(d_ff_16_nq), .C(button_17_out), .Q(IC7_pin6[0]), .nQ(d_ff_16_nq));
  Button button_16 (.out(button_16_out));
  Seven_Seg_Hex seven_seg_hex_9 (.d(d_ff_9_q), .dp(1'b0));
  Button button_17 (.out(button_17_out));
  Seven_Seg_Hex seven_seg_hex_10 (.d(IC7_pin6), .dp(1'b0));
  _74299 IC6 (
    .pin1(in_9), .pin2(in_10), .pin3(in_11), .pin4(IC6_pin5[2]), .pin5(IC6_pin5[0]), .pin6(IC6_pin6[2]),
    .pin7(IC6_pin6[0]), .pin8(IC5_pin18), .pin9(1'b1), .pin10(1'b0), .pin11(in_12), .pin12(IC3_pin8),
    .pin13(IC6_pin6[1]), .pin14(IC6_pin6[3]), .pin15(IC6_pin5[1]), .pin16(IC6_pin5[3]), .pin18(IC5_pin8),
    .pin19(IC13_pin15), .pin20(1'b1));  // open: pin17
  LED led_25 (.in(IC6_pin5[3]));
  LED led_26 (.in(IC6_pin5[2]));
  LED led_27 (.in(IC6_pin5[1]));
  LED led_28 (.in(IC6_pin5[0]));
  LED led_29 (.in(IC6_pin6[3]));
  LED led_30 (.in(IC6_pin6[2]));
  LED led_31 (.in(IC6_pin6[1]));
  Seven_Seg_Hex seven_seg_hex_11 (.d(IC6_pin5), .dp(1'b0));
  LED led_32 (.in(IC6_pin6[0]));
  // Probe LATCH on IC13_pin15
  // Probe SCK on IC3_pin8
  // Probe MISO on IC5_pin18
  // Probe MOSI on IC5_pin8
  Seven_Seg_Hex seven_seg_hex_12 (.d(IC6_pin6), .dp(1'b0));

  // Notes on the sheet:
  //   CLK: Hz: 2
  //   TRIG
  //   SPI Sequencer
  //   SS
  //   SCK
  //   B Register
  //   Enter B
  //   Switch Input Register
  //   Slave Register
  //   S1     S0       MODE
  //   0          0       HOLD
  //   0          1       RIGHT
  //   1          0       LEFT
  //   1          1       LOAD
  //   LATCH
  //   Load
  //   Master Register
  //   Load Master Register
endmodule
