// Digital circuit 299_master_slave.dig as structural Verilog
module _299_master_slave (
);

  wire IC1_p2, IC1_p3, IC1_p4;

  // _74299 IC1: pin names not known; wires that end beside it: 1'b1, IC1_p2, IC1_p3, IC1_p4, 1'b0
  // _74299 IC2: pin names not known; wires that end beside it: 1'b1, IC1_p3, IC1_p2, IC1_p4, 1'b0

  // Notes on the sheet:
  //   Connecting a pair of 74299 shift registers as Master-Slave
  //   Master
  //   SCK
  //   MOSI
  //   MISO
  //   Slave
endmodule
